# Fritzing sketch KevinMorseCodeEncoderPlusDecoder (saved by Fritzing 0.9.3b)
breadboards: 1

parts:
  Part1 = Arduino Uno (Rev3)
  S1 = Pushbutton [package="[THT]"]
  LED1 = LED - 5mm [color="Red (633nm)" package="5 mm [THT]"]
  R1 = Resistor [tolerance=±5% resistance=220 package=THT]
  R2 = Resistor [tolerance=±5% resistance=220 package=THT]
  SG1 = Buzzer 12mm [package=buzzer-12mm-ns]
  S2 = Pushbutton [package="[THT]"]

nets:
  N1: Part1.D12/MISO, S2.Pin_3, S2.Pin_4
  N2: Part1.GND, S1.Pin_3, S1.Pin_4, SG1.2
  N3: Part1.D2, S1.Pin_1, S1.Pin_2
  N4: Part1.D3_PWM, R2.Pin_1
  N5: Part1.D7, LED1.anode
  N6: Part1.5V, R1.Pin_1, S2.Pin_1, S2.Pin_2
  N7: LED1.cathode, R1.Pin_0
  N8: R2.Pin_0, SG1.1

notes:
  Morse Code Encoder and Decoder
